# Fritzing sketch Temperatur LCD (saved by Fritzing 0.9.4)
breadboards: 1

parts:
  Arduino_Uno_R3 = Arduino Uno (Rev3)
  DHT11_Sensor = KY-015 Temperature & Humidity Sensor Module [package="Breakout board"]
  R1 = Rotary Potentiometer (Large) [maximum_resistance=10kΩ package=THT]
  LCD1602_Module = LCD-16X2 [package=lcd-16x2_nosilk]

nets:
  N1: Arduino_Uno_R3.D8, LCD1602_Module.RS
  N2: Arduino_Uno_R3.D9_PWM, LCD1602_Module.E
  N3: Arduino_Uno_R3.D10_PWM/SS, LCD1602_Module.DB4
  N4: Arduino_Uno_R3.D11_PWM/MOSI, LCD1602_Module.DB5
  N5: Arduino_Uno_R3.D12/MISO, LCD1602_Module.DB6
  N6: Arduino_Uno_R3.D13/SCK, LCD1602_Module.DB7
  N7: Arduino_Uno_R3.D7, DHT11_Sensor.S
  5V: Arduino_Uno_R3.5V, DHT11_Sensor.Vin, R1.leg1, LCD1602_Module.VSS, LCD1602_Module.VDD, LCD1602_Module.A, LCD1602_Module.K
  N8: Arduino_Uno_R3.GND, DHT11_Sensor.-, R1.leg2, LCD1602_Module.R_W
  N9: R1.wiper, LCD1602_Module.VO

custom parts:
  KY-015 Temperature & Humidity Sensor Module: KY-015 temperature and humidity sensor module, provides a low-latency serial interface to measure humidity and temperature.
